# Fritzing sketch Cup (saved by Fritzing 0.9.2b)
breadboards: 1

parts:
  元件2 = Intel Galileo
  元件4 = SRF05 Ultrasonic Rangefinder
  KY-2 = Keyes Relay [package=THT]
  元件5 = Ambient Light Sensor (TEMT6000 Breakout Board)
  M1 = DC Motor
  LCD2 = LCD screen
  LCM1602_IIC2 = LCM1602 IIC [part_number="LCM1602 IIC" chip_label="LCM1602 IIC" package="DIP (Dual Inline) [THT]"]

nets:
  N1: 元件2.A4/SDA, LCM1602_IIC2.SDA
  N2: 元件2.A5/SCL, LCM1602_IIC2.SCL
  N3: 元件2.D2, 元件4.Trig
  N4: 元件2.D3_PWM, 元件4.Echo
  N5: 元件2.D4, KY-2.signal
  N6: 元件2.D5_PWM, 元件5.S
  VCC: 元件2.5V, 元件4.VCC, KY-2.power, KY-2.C, 元件5.VCC, LCM1602_IIC2.VCC
  GND: 元件2.GND, 元件4.GND, KY-2.ground, 元件5.GND, M1.pin_2, LCM1602_IIC2.GND
  N7: KY-2.NO, M1.pin_1
  VSS: LCD2.VSS, LCM1602_IIC2.VSS
  VDD: LCD2.VDD, LCM1602_IIC2.VDD
  N8: LCD2.V0, LCM1602_IIC2.V0
  N9: LCD2.RS, LCM1602_IIC2.RS
  N10: LCD2.R/W, LCM1602_IIC2.RW
  N11: LCD2.E, LCM1602_IIC2.E
  N12: LCD2.DB0, LCM1602_IIC2.D0
  N13: LCD2.DB1, LCM1602_IIC2.D1
  N14: LCD2.DB2, LCM1602_IIC2.D2
  N15: LCD2.DB3, LCM1602_IIC2.D3
  N16: LCD2.DB4, LCM1602_IIC2.D4
  N17: LCD2.DB5, LCM1602_IIC2.D5
  N18: LCD2.DB6, LCM1602_IIC2.D6
  N19: LCD2.DB7, LCM1602_IIC2.D7
  N20: LCD2.LED+, LCM1602_IIC2.A
  N21: LCD2.LED-, LCM1602_IIC2.K
  N22: LCM1602_IIC2.LED_A, LCM1602_IIC2.LED_B

custom parts:
  Keyes Relay: The Keyes 5V relay module is suitable for SCM development, home appliance control. It uses a 5V~12V TIL control signal which can control DC / AC signal.
  LCM1602 IIC: I2C-Module to use a 1602 or 2004 LCD on with the wire.h libory Serial LCD Modul
